# Fritzing sketch CodificadorConvolucionalDiagrama (saved by Fritzing 0.9.2b)
breadboards: 1

parts:
  Parte1 = Arduino Uno (Rev3)
  LED2 = LED - 3mm [color="Red (633nm)" package="3 mm [THT]"]
  LED3 = LED - 3mm [color="Red (633nm)" package="3 mm [THT]"]
  LED4 = LED - 3mm [color="Red (633nm)" package="3 mm [THT]"]
  LED5 = LED - 3mm [color="Red (633nm)" package="3 mm [THT]"]
  LED6 = LED - 3mm [color="Red (633nm)" package="3 mm [THT]"]
  LED7 = LED - 3mm [color="Red (633nm)" package="3 mm [THT]"]
  LED8 = LED - 3mm [color="Red (633nm)" package="3 mm [THT]"]
  R1 = Resistor [tolerance=±5% resistance=220 package="0805 [SMD]"]
  R2 = Resistor [tolerance=±5% resistance=220 package="0805 [SMD]"]
  R3 = Resistor [tolerance=±5% resistance=220 package="0805 [SMD]"]
  R4 = Resistor [tolerance=±5% resistance=220 package="0805 [SMD]"]
  R5 = Resistor [tolerance=±5% resistance=220 package="0805 [SMD]"]
  R6 = Resistor [tolerance=±5% resistance=220 package="0805 [SMD]"]
  R7 = Resistor [tolerance=±5% resistance=220 package="0805 [SMD]"]
  R8 = Resistor [tolerance=±5% resistance=220 package="0805 [SMD]"]
  SW1 = DIP Switch 8 Position [package=dipswitch-08]
  LED1 = LED - 3mm [color="Red (633nm)" package="3 mm [THT]"]

nets:
  N1: Parte1.A0, Parte1.A1, Parte1.A2, Parte1.A3, Parte1.GND, R1.Pin_0, R2.Pin_0, R3.Pin_0, R4.Pin_0, R5.Pin_0, R6.Pin_0, R7.Pin_0, R8.Pin_0, SW1.13, SW1.14, SW1.15, SW1.16
  N2: Parte1.D8, LED2.cathode
  N3: Parte1.D9_PWM, LED1.cathode
  N4: Parte1.D2, LED8.cathode
  N5: Parte1.D3_PWM, LED7.cathode
  N6: Parte1.D4, LED6.cathode
  N7: Parte1.D5_PWM, LED5.cathode
  N8: Parte1.D6_PWM, LED4.cathode
  N9: Parte1.D7, LED3.cathode
  N10: LED2.anode, R2.Pin_1
  N11: LED3.anode, R3.Pin_1
  N12: LED4.anode, R4.Pin_1
  N13: LED5.anode, R5.Pin_1
  N14: LED6.anode, R6.Pin_1
  N15: LED7.anode, R7.Pin_1
  N16: LED8.anode, R8.Pin_1
  N17: R1.Pin_1, LED1.anode

// code stored in the sketch: codeCodificadorCon.ino
/*
  Andres Infante Torres
  Codificador Convolucional
*/


//arreglo de lectura dipswitch
int val[4];
//arreglo para corrimiento [][][]
int secIn[3];
//arreglo de salida secuencia codificada 8 bits
int secOut[8];


int i = 0, j = 0;
int cont = 3; //cont para corrimento [][][]
int contOut = 0; //con para salida

//pines de output LEDS
int oPin[] = {2, 3, 4, 5, 6, 7, 8, 9};


void setup() {

  //leds declaracion de salidas leds
  for (i = 0; i < 8; i++) {
    pinMode(oPin[i], OUTPUT);
  }

  //switch DIP declaracion de entradas
  pinMode(A0, INPUT_PULLUP);
  pinMode(A1, INPUT_PULLUP);
  pinMode(A2, INPUT_PULLUP);
  pinMode(A3, INPUT_PULLUP);

  //para monitor (debuguear)
  //Serial.begin(9600);

}



void loop() {
  //inicializa Secuencia de entrada [][][] en 0
  for (i = 0; i < 3; i++) {
    secIn[i] = 0;
    //inicializa los valores
    val[i] = 0;
  }
  //inicializa sec salida 8 bits
  for (i = 0; i < 8; i++) {
    secOut[i] = 0;
  }

  //obteniendo valores del dip switch
  val[0] = digitalRead(A0);
  val[1] = digitalRead(A1);
  val[2] = digitalRead(A2);
  val[3] = digitalRead(A3);

  // debuguear entrada del dip
  //  Serial.println("inicio: ");
  //  for (i = 0; i < 4; i++)
  //    Serial.println(val[i]);

  //probar que enciendan todos los leds
  //  for (i = 0; i < 8; i++)
  //  digitalWrite(oPin[i], HIGH);

  cont = 3;
  contOut = 0;


  //mientras entren los 4bits a la secuencia de entrada
  while (cont >= 0) {
    //recorrer secuencia de entrada 1 posicion para poner un bit nuevo
    for (i = 0; i < 3; i++) {
      if (i != 2) { //ya que se recorrieron los primeros 2
        secIn[i] = secIn[i + 1];
      }
      else { //se pone un bit de la entrada
        secIn[i] = val[cont];
        cont--;
      }
    }

    //si se llenaron los 8 bits de salida recorrer para dejar 2 libres al final
    if (contOut == 8) {
      for (j = 0; j < 6; j++) {
        secOut[j] = secOut[j + 2];
      }
      contOut = 6;
    }

    //agregando bits a la salida
    //si el ultimo bit y el segundo son iguales se pone 0
    if ((secIn[2] == 0 && secIn[1] == 0) || (secIn[2] == 1 && secIn[1] == 1)) {
      secOut[contOut] = 0;
      contOut++;
    }
    else {//sino 1
      secOut[contOut] = 1;
      contOut++;
    }

    //si el ultimo y el primero son iguales se pone 0
    if ((secIn[2] == 0 && secIn[0] == 0) || (secIn[2] == 1 && secIn[0] == 1)) {
      secOut[contOut] = 0;
      contOut++;
    }
    else {//sino 1
      secOut[contOut] = 1;
      contOut++;
    }

    //aviso de que mostrara iteracion
    for (i = 0; i < 8; i++)
      digitalWrite(oPin[i], HIGH);
    delay(1000);

    //mostrando resultados
    for (j = 0; j < 8; j++) {
      if (secOut[j] == 0)
        digitalWrite(oPin[j], LOW);
      else
        digitalWrite(oPin[j], HIGH);
    }

    delay(5000);
  }

  //al final apagar los leds y esperar nueva entrada
  for (j = 0; j < 8; j++) {
    digitalWrite(oPin[j], LOW);
  }
  delay(10000);

}
